# Fritzing sketch MKR1500-v250814 (saved by Fritzing 0.9.10b)
circuit board: 24.8567cm x 17.636cm

parts:
  Part1 = Adafruit_BMP280
  Part2 = MCP9808 High Accuracy I2C Temperature Sensor [part_number=1782]
  Part3 = HTU21D-F Temperature + Humidity Sensor
  C1 = Ceramic Capacitor [capacitance=0.1mF package="100 mil [THT, multilayer]"]
  R2 = Resistor [tolerance=±5% resistance=1k power=0.25 package=THT]
  C2 = Ceramic Capacitor [capacitance=0.1mF package="100 mil [THT, multilayer]"]
  U4 = Honeywell SS451A [chip_label="Hall Effect Sensor" package=THT]
  U7 = Honeywell SS451A [chip_label="Hall Effect Sensor" package=THT]
  Part12 = OLED Monochrome 128x32 I2C [part_number=931]
  Part15 = Adafruit BME280
  Part16 = Adafruit RFM9x LoRa Radio [part_number="Adafruit #3072 and #3073"]
  Part17 = Arduino MKR NB 1500
  Part18 = Adafruit DS3231 [part_number="Adafruit #3013"]
  S1 = Toggle Switch [package=THT]  # not connected
  Part20 = Adafruit SDIO microSD Breakout
  Part4 = SI1145 Digital UV Index + IR + Visible Light Sensor [part_number=1777]
  R1 = Resistor [tolerance=±5% power=0.25 resistance=1k package=THT]
  R3 = Resistor [tolerance=±5% power=0.25 resistance=220 package=THT]  # not connected
  Adafruit_24LC32_I2C_EEPROM2 = Adafruit 24LC32 I2C EEPROM Breakout - 32Kbit / 4 KB - Stemma QT [part_number=#5146]  # not connected
  X3 = USB Connectors [package=usb-a-s-nosilk-female]  # not connected
  JP5 = Header 2 [package=jst-2-pth-ns]  # not connected
  JP6 = Header 2 [package=jst-2-pth-ns]  # not connected
  Part21 = USB Mini-B Breakout [part_number=1764]  # not connected
  BAT3 = Battery Holders [package=lipo-1100mAh]  # not connected
  Adafruit_24LC32_I2C_EEPROM3 = Adafruit 24LC32 I2C EEPROM Breakout - 32Kbit / 4 KB - Stemma QT [part_number=#5146]
  OLED_I2C4 = OLED 128x64 I2C Monochrome Display  # not connected
  Part29 = Adafruit BMP280 [part_number="Adafruit #2651"]
  Part30 = Adafruit BMP388 [part_number="Adafruit #3966"]
  Part31 = Adafruit BME280 [part_number="Adafruit #2652"]
  Part32 = Adafruit MCP9808 [part_number="Adafruit #5027"]
  Part33 = Adafruit HTU21D-F Temperature & Humidity Sensor [part_number="Adafruit #1899"]
  Part34 = Adafruit SHT31-D [part_number="Adafruit #2857"]
  Part35 = OLED Monochrome 128x32 I2C [part_number=931]  # not connected
  Part36 = SI1145 Digital UV Index + IR + Visible Light Sensor [part_number=1777]  # not connected
  Part28 = Adafruit PA1010D Mini GPS Module [part_number="Adafruit #4415"]

nets:
  VIN: Part1.VIN, Part15.VIN
  GND: Part1.GND, Part2.GND, Part3.GND, Part15.GND
  N1: Part1.SCK/SCL, Part2.SCL, Part3.SCL, Part12.SCL, Part15.SCK/SCL, Part17.D12~/MISO, Part18.SCL
  VIN_2: Part1.SDI/SDA, Part2.VDD, Part2.SDA, Part3.VIN, Part3.SDA, Part12.VIN, Part12.SDA, Part15.SDI/SDA, Part17.D11/MOSI, Part17.+5V, Part18.Vin, Part18.SDA, Part4.+5V
  N2: C1.0, C2.0, U4.pin2, U7.pin2, Part16.GND
  N3: C1.1, R1.Pin_0
  N4: R2.Pin_0, C2.1, U4.pin1, U7.pin1, Part16.VIN
  N5: R2.Pin_1, U4.pin3, Part17.A2
  N6: U7.pin3, Part17.A1, R1.Pin_1
  GND_2: Part12.GND, Part18.GND
  N7: Part16.DIO0, Part17.D7
  N8: Part16.SCK, Part17.D3~
  N9: Part16.MISO, Part17.A3
  N10: Part16.MOSI, Part17.D2
  N11: Part16.CS, Part17.D5~
  N12: Part16.RST, Part17.A4
  N13: Part17.D0, Part4.SDA
  N14: Part17.D1, Part4.SCL
  GND_3: Part17.GND, Part20.GND, Part4.GND
  N15: Part17.D4, Part20.CS
  N16: Part17.D8, Part20.DO
  N17: Part17.D9~, Part20.SCLK
  N18: Part17.D10~, Part20.DI
  +3V3: Part17.+3V3, Part20.3.3V
  GND_4: Adafruit_24LC32_I2C_EEPROM3.GND, Part29.GND, Part30.GND, Part31.GND, Part32.GND, Part33.GND, Part34.GND, Part28.GND
  VCC: Adafruit_24LC32_I2C_EEPROM3.VCC, Part29.VCC, Part30.VCC, Part31.VCC, Part32.VCC, Part33.VCC, Part34.VCC, Part28.VCC
  N19: Adafruit_24LC32_I2C_EEPROM3.SDA, Part29.SDI/SDA, Part30.SDI/SDA, Part31.SDI/SDA, Part32.SDA, Part33.SDA, Part34.SDA, Part28.SDA
  N20: Adafruit_24LC32_I2C_EEPROM3.SCL, Part29.SCK/SCL, Part30.SCK/SCL, Part31.SCK/SCL, Part32.SCL, Part33.SCL, Part34.SCL, Part28.SCL

notes:
  MCP9808 High Accuracy Temperature Sensor
  I2C 7-bit address 0x18
  HTU21D-F Temperature & Humidity Sensor
  I2C 7-bit address 0x40
  Anemometer (Wind Speed)
  SS451A Omnipolar Digital Hall-effect Sensor
  Pin A2
  Wind Vane (as5600-so_ek_ab)
  AS5600 Rotory Position Sensor
  I2C 7-bit address 0x36
  Adafruit SI1145
  Light Sensor
  I2C 7-bit address 0x60
  Rain Gauge
  SS451A Omnipolar Digital Hall-effect Sensor
  Pin A1
  MKR NB 1500 Full Station Schematic v2025-08-14
  RFM9x LoRa Radio
  MISO to A3 SPI1 MISO
  MOSI to D2 SPI1 MOSI
  SCK to D3 SPI1 SCK
  CS to D5 CS
  RESET to A4
  DIO0 to D7
  Adafruit OLED 128x32
  Display SSD1306<module
  I2C 7-bit address 0x3C
  Console Enable Switch
  Pin A4 to Ground
  MKR SD Proto Board
  Pin D4 SD Chip Select
  Pin D10 MISO
  Pin D9 SCK
  Pin D8 MOSI
  D14/TX =
  D13/RX =
  D12/SCL = Wire I2C
  D11/SDA = Wire I2C
  D10MISO = SD Card
  D9/SCK = SD Card
  D8*/MOSI = SD Card
  D7* = Interrupt LoRa DIO0
  D6* = On Board LED
  A0 = WatchDog Reset Trigger
  A1* = Interrupt For Rain Gauge
  A2* = Interrupt For Anemometer (Wind Speed)
  A3 = SPI1 MISO LoRa
  A4 = Serial Console (Ground Pin to Enable)
  A5 = LoRa Reset
  A6 = WatchDog Monitor Heartbeat
  D0* = Wire1 I2C/SDA SI1145
  D1* = Wire1 I2C/CLK SI1145
  D2 = SPI1 MOSI LoRa
  D3 = SPI1CLK LoRa
  D4* = SD Card Chip Select
  D5* = Lora CS
  * = Interrupt Supported Pin
  BMP280
  Barometic Pressure
  Altitude Sensor
  Temperature
  I2C 7-bit address
  Default = 0x77
  SD0 to GND = 0x76
  BME280
  Barometic Pressure
  Altitude Sensor
  Temperature
  Humidity
  I2C 7-bit address
  Default = 0x76
  SD0 to GND = 0x77
  Software supports
  BMP or BME at 0x77
  BMP or BME at 0x76
  Adafruit DS3231
  RTC
  I2C 7-bit address 0x68
  BQ24195L on board MKR NB 1500
  2.5-A /4.5-A SingleCell USB/AdapterCharger
  I2C 7-bit address 0x6B
  ECC508 on board MKR NB 1500
  Crypto Auth Chip
  I2C address 0x60
  Wire1 I2C Bus
  Wire0 I2C Bus
  Micro USB- 5V DC Relay
  Micro USB+ Time Delay
  NC
  Trigger COM
  V- NO
  P817 Optocoupler VCC
  Input+ OUT
  Input - GND
  24LC32 I2C EEPROM
  I2C address 0x50
  5V TR TR HB
  WatchDog Monitor
  BME288
  Barometic Pressure
  Altitude Sensor
  Temperature
  Humidity
  I2C 7-bit address
  Default = 0x76
  SD0 to GND = 0x77
  BMP388
  Barometic Pressure
  Altitude Sensor
  Temperature
  I2C 7-bit address
  Default = 0x77
  SD0 to GND = 0x76
  Adafruit OLED64
  Display SSD1306
  I2C 7-bit address 0x3D
  Adafruit OLED 128x32
  Display SSD1306
  I2C 7-bit address 0x3C
  Only one OLED at a time
  HIH8000 Temperature & Humidy
  I2C address 0x27
  SHT31 Temperature & Humidy
  I2C address 0x44
  I2C address 0x45 ADR Pin High

custom parts:
  Adafruit_BMP280: Bosch has stepped up their game with their new BMP280 sensor, an environmental sensor with temperature, barometric pressure that is the next generation upgrade to the BMP085/BMP180/BMP183. This sensor is great for all sorts of weather sensing and can even be used in both I2C and SPI! This precision sensor from Bosch is the best low-cost, precision sensing solution for measuring barometric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
  MCP9808 High Accuracy I2C Temperature Sensor: This I2C digital temperature sensor is one of the more accurate/precise we've ever seen, with a typical accuracy of ±0.25°C over the sensor's -40°C to +125°C range and precision of +0.0625°C. They work great with any microcontroller using standard i2c. There are 3 address pins so you can connect up to 8 to a single I2C bus without address collisions. Best of all, a wide voltage range makes is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
  HTU21D-F Temperature + Humidity Sensor: This I2C digital humidity sensor is an accurate and intelligent alternative to the much simpler Humidity and Temperature Sensor - SHT15 Breakout It has a typical accuracy of ±2% with an operating range that's optimized from 5% to 95% RH. Operation outside this range is still possible - just the accuracy might drop a bit. The temperature output has an accuracy of ±1°C from -30~90°C. If you're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
  Honeywell SS451A: Omnipolar Digital Hall-effect Sensor
  OLED Monochrome 128x32 I2C: These displays are small, only about 1" diagonal, but very readable due to the high contrast of an OLED display. This display is made of 128x32 individual white OLED pixels, each one is turned on or off by the controller chip. Because the display makes its own light, no backlight is required. This reduces the power required to run the OLED and is why the display has such high contrast; we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
  Adafruit BME280: Bosch has stepped up their game with their new BME280 sensor, an environmental sensor with temperature, barometric pressure and humidity! This sensor is great for all sorts of weather/environmental sensing and can even be used in both I2C and SPI! This precision sensor from Bosch is the best low-cost sensing solution for measuring humidity with ±3% accuracy, barometric pressure with ±1 hPa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
  Adafruit RFM9x LoRa Radio: Sending data over long distances is like magic, and now you can be a magician with this range of powerful and easy-to-use radio modules. Sure, sometimes you want to talk to a computer (a good time to use WiFi) or perhaps communicate with a Phone (choose Bluetooth Low Energy!) but what if you want to send data very far? Most WiFi, Bluetooth, Zigbee and other wireless chipsets use 2.4GHz, which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
  Arduino MKR NB 1500: Add Narrowband communication to your project with the MKR NB 1500. It's the perfect choice for devices in remote locations without an Internet connection, or in situations in which power isn't available like on-field deployments, remote metering systems, solar-powered devices, or other extreme scenarios. The board's main processor is a low power Arm® Cortex®-M0 32-bit SAMD21, like in the other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
  Adafruit DS3231: The datasheet for the DS3231 explains that this part is an "Extremely Accurate I²C-Integrated RTC/TCXO/Crystal". And, hey, it does exactly what it says on the tin! This Real Time Clock (RTC) is the most precise you can get in a small, low power package. Most RTCs use an external 32kHz timing crystal that is used to keep time with low current draw. And that's all well and good, but those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
  SI1145 Digital UV Index + IR + Visible Light Sensor: The SI1145 is a new sensor from SiLabs with a calibrated light sensing algorithm that can calculate UV Index. It doesn't contain an actual UV sensing element, instead it approximates it based on visible & IR light from the sun. We took this outside a couple days and compared the calculated UV index with the news-reported index and found it was very accurate! It's a digital sensor that works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
  Adafruit 24LC32 I2C EEPROM Breakout - 32Kbit / 4 KB - Stemma QT: If you want to store calibration values, MAC addresses, non-secure access tokens, or other unique identifiers, EEPROM storage is a great option. EEPROM is long lasting, and doesn't need to be written in pages - a single byte can be written at once (unlike with flash memory!) EEPROM storage persists even when the power goes out, and can be over-written literally one million times. Some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
  USB Mini-B Breakout: Simple but effective - this breakout board has a USB Mini-B connector, with all 5 pins broken out. Great for pairing with a microcontroller with USB support, or adding USB 5V power to a project.
  Adafruit BMP280: Bosch has stepped up their game with their new BMP280 sensor, an environmental sensor with temperature, barometric pressure that is the next generation upgrade to the BMP085/BMP180/BMP183. This sensor is great for all sorts of weather sensing and can even be used in both I2C and SPI! This precision sensor from Bosch is the best low-cost, precision sensing solution for measuring barometric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
  Adafruit BMP388: Bosch has been a leader in barometric pressure sensors, from the BMP085. BMP180, and BMP280... now we've got the next generation, the Adafruit BMP388 Precision Barometric Pressure sensor. As you would expect, this sensor is similar to its earlier versions but even better. The BMP388 has better precision than ever, which makes it excellent for environmental sensing or as a precision altimeter.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
  Adafruit BME280: Bosch has stepped up their game with their new BME280 sensor, an environmental sensor with temperature, barometric pressure and humidity! This sensor is great for all sorts of indoor environmental sensing and can even be used in both I2C and SPI! This precision sensor from Bosch is the best low-cost sensing solution for measuring humidity with ±3% accuracy, barometric pressure with ±1 hPa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
  Adafruit MCP9808: The MCP9808 digital temperature sensor is one of the more accurate/precise we've ever seen, with a typical accuracy of ±0.25°C over the sensor's -40°C to +125°C range and precision of +0.0625°C. They work great with any microcontroller using standard I2C. With three address jumpers on the back, you can connect up to 8 to a single I2C bus without address collisions. Best of all, a wide voltage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
  Adafruit HTU21D-F Temperature & Humidity Sensor: It's summer and you're sweating and your hair's all frizzy and all you really want to know is why the weatherman said this morning that today's relative humidity would max out at a perfectly reasonable 52% when it feels more like 77%. Enter the HTU21D-F Temperature + Humidity Sensor - the best way to prove the weatherman wrong! This I2C digital humidity sensor is an accurate and intelligent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
  Adafruit SHT31-D: Sensirion Temperature/Humidity sensors are some of the finest & highest-accuracy devices you can get. And, finally we have some that have a true I2C interface for easy reading. The SHT31-D sensor has an excellent ±2% relative humidity and ±0.3°C accuracy for most uses. We now use the version with a PTFE filter, it'll stay clean while still allowing humidity measurements to work Unlike earlier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
  Adafruit PA1010D Mini GPS Module: This miniature GPS breakout is only 1" x 1" (~ 25mm x 25mm) but houses a complete GPS/GNSS solution with both I2C and UART interfaces. There's even an antenna on top so it's plug and play! Support for GPS, GLONASS, GALILEO, QZSS -165 dBm sensitivity, up to 10 Hz updates Up to 210 PRN channels with 99 search channels and 33 simultaneous tracking channels 5V friendly design and only 30mA current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
